# Fritzing sketch Sketch_ArduinoUno (saved by Fritzing 0.9.3b)
circuit board: 8.46667cm x 5.64444cm
breadboards: 3

parts:
  Squix1 = OLED 0.96" 128x64 I2C SSD1306
  Squix2 = OLED 0.96" 128x64 I2C SSD1306
  Squix3 = OLED 0.96" 128x64 I2C SSD1306
  Squix4 = OLED 0.96" 128x64 I2C SSD1306
  Componente1 = Adafruit DS3231 [part_number="Adafruit #3013"]
  Componente2 = Arduino Uno (Rev3)
  S1 = Pushbutton [package="[THT]"]
  S2 = Pushbutton [package="[THT]"]
  S3 = Pushbutton [package="[THT]"]
  S4 = Pushbutton [package="[THT]"]
  BT1 = Bluetooth HC-06u [package=THT]
  J1 = Piezo Speaker

nets:
  VCC: Squix1.VCC, Squix2.VCC, Squix3.VCC, Squix4.VCC, Componente2.3V3, BT1.VCC
  GND: Squix1.GND, Squix2.GND, Squix3.GND, Squix4.GND, Componente1.GND, Componente2.GND, S1.Pin_1, S1.Pin_2, S2.Pin_1, S2.Pin_2, S3.Pin_1, S3.Pin_2, S4.Pin_1, S4.Pin_2, BT1.GND, J1.pin1
  N1: Squix1.SCL, Squix2.SCL, Squix3.SCL, Squix4.SCL, Componente1.SCL, Componente2.A5/SCL
  N2: Squix1.SCA, Squix2.SCA, Squix3.SCA, Squix4.SCA, Componente1.SDA, Componente2.A4/SDA
  VIN: Componente1.Vin, Componente2.5V
  N3: Componente2.D8, S1.Pin_3, S1.Pin_4
  N4: Componente2.D9_PWM, S2.Pin_3, S2.Pin_4
  N5: Componente2.D10_PWM/SS, S3.Pin_3, S3.Pin_4
  N6: Componente2.D11_PWM/MOSI, S4.Pin_3, S4.Pin_4
  N7: Componente2.D2, BT1.RXD
  N8: Componente2.D3_PWM, BT1.TXD
  N9: Componente2.D6_PWM, J1.pin2

custom parts:
  Adafruit DS3231: The datasheet for the DS3231 explains that this part is an "Extremely Accurate I²C-Integrated RTC/TCXO/Crystal". And, hey, it does exactly what it says on the tin! This Real Time Clock (RTC) is the most precise you can get in a small, low power package. Most RTCs use an external 32kHz timing crystal that is used to keep time with low current draw. And that's all well and good, but those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
  Bluetooth HC-06u: Bluetooth HC-06 - face up, pins down 16.5mm x 37.5mm PCB
